# Fritzing sketch Wiring (saved by Fritzing 0.9.3b)
breadboards: 2

parts:
  Part1 = Arduino Mega 2560 (Rev3)
  Part2 = LCD1602-I2C
  S1 = KY-026
  J1 = Basic Servo
  Part3 = Thumb Joystick
  Part4 = RFID-RC522-v2
  HC-SR04_Sensor_1 = HC-SR04 Ultrasonic Distance Sensor
  Matrix_keypad1 = KEYPAD 4x4  # not connected

nets:
  N1: Part1.A0, S1.pin1
  N2: Part1.A1, Part3.VERT
  N3: Part1.A2, Part3.HORZ
  N4: Part1.SCL, Part2.SCL
  N5: Part1.SDA, Part2.SDA
  N6: Part1.D9_PWM, Part4.SDA
  N7: Part1.D8_PWM, Part4.RST
  3V3: Part1.3V3, Part4.3.3V
  GND: Part1.GND, Part4.GND
  N8: Part1.D2_PWM, J1.pulse
  N9: Part1.D3_PWM, Part3.SEL
  N10: Part1.D6_PWM, HC-SR04_Sensor_1.ECHO
  N11: Part1.D7_PWM, HC-SR04_Sensor_1.TRIG
  N12: Part1.D22, S1.pin4
  N13: Part1.D50, Part4.MOSI
  N14: Part1.D51, Part4.MISO
  N15: Part1.D52, Part4.SCK
  GND_2: Part2.GND, S1.pin2, J1.gnd, Part3.GND, HC-SR04_Sensor_1.GND
  VCC: Part2.VCC, S1.pin3, J1.vcc, Part3.VCC, HC-SR04_Sensor_1.VCC

custom parts:
  LCD1602-I2C: A standard character display, usually with 2x16 characters. Comes in many colors with LCM1602 IIC attached.
  KY-026: ky-026 flame sensor module
  RFID-RC522-v2: A simple China made RFID-RC522 Reader; do check the pin labels, as this is a MFRC522 based clone.
  KEYPAD 4x4: Matrix keypad 16 buttons, 4 rows x 4 columns
